// Logisim project Aula1.circ as structural Verilog: 3 circuits, main circuit main
module main (
  input  in_1,
  input  in_2,
  input  in_3,
  input  in_4,
  input  SAVE,
  input  reset,
  output out_7,
  output out_8,
  output out_9,
  output out_10
);

  D_Flip_Flop d_ff_1 (.clk(in_2), .D(in_1), .Q(out_7), .reset(reset));  // open: Qn, preset, en
  D_Flip_Flop d_ff_2 (.clk(in_2), .D(in_2), .Q(out_8), .reset(reset));  // open: Qn, preset, en
  D_Flip_Flop d_ff_3 (.clk(in_2), .D(in_2), .Q(out_9), .reset(reset));  // open: Qn, preset, en
  D_Flip_Flop d_ff_4 (.clk(in_2), .D(in_3), .Q(out_10), .reset(reset));  // open: Qn, preset, en

  assign in_4 = in_2;
  assign SAVE = in_2;
endmodule

module fp4bit (
  input  [3:0] INPUT,
  input  SAVE,
  input  reset,
  output [3:0] OUT
);

  D_Flip_Flop d_ff_1 (.clk(INPUT[2]), .D(INPUT[3]), .Q(OUT[3]), .reset(reset));  // open: Qn, preset, en
  D_Flip_Flop d_ff_2 (.clk(INPUT[2]), .D(INPUT[2]), .Q(OUT[2]), .reset(reset));  // open: Qn, preset, en
  D_Flip_Flop d_ff_3 (.clk(INPUT[2]), .D(INPUT[2]), .Q(OUT[1]), .reset(reset));  // open: Qn, preset, en
  D_Flip_Flop d_ff_4 (.clk(INPUT[2]), .D(INPUT[1]), .Q(OUT[0]), .reset(reset));  // open: Qn, preset, en

  assign INPUT[0] = INPUT[2];
  assign SAVE = INPUT[2];
endmodule

module fp8Bit (
  input  [3:0] in_1
);

  wire demultiplexer_1_out0, demultiplexer_1_out1, demultiplexer_1_out2, demultiplexer_1_out3,
       demultiplexer_1_out4, demultiplexer_1_out5, demultiplexer_1_out6, demultiplexer_1_out7;

  Demultiplexer #(.select(3)) demultiplexer_1 (
    .out0(demultiplexer_1_out0), .out1(demultiplexer_1_out1), .out2(demultiplexer_1_out2),
    .out3(demultiplexer_1_out3), .out4(demultiplexer_1_out4), .out5(demultiplexer_1_out5),
    .out6(demultiplexer_1_out6), .out7(demultiplexer_1_out7));  // open: in, sel, en
  fp4bit fp4bit_1 (.SAVE(demultiplexer_1_out0), .INPUT(in_1));  // open: reset, OUT
  fp4bit fp4bit_2 (.SAVE(demultiplexer_1_out1), .INPUT(in_1));  // open: reset, OUT
  fp4bit fp4bit_3 (.SAVE(demultiplexer_1_out2), .INPUT(in_1));  // open: reset, OUT
  fp4bit fp4bit_4 (.SAVE(demultiplexer_1_out3), .INPUT(in_1));  // open: reset, OUT
  fp4bit fp4bit_5 (.SAVE(demultiplexer_1_out4), .INPUT(in_1));  // open: reset, OUT
  fp4bit fp4bit_6 (.SAVE(demultiplexer_1_out5), .INPUT(in_1));  // open: reset, OUT
  fp4bit fp4bit_7 (.SAVE(demultiplexer_1_out6), .INPUT(in_1));  // open: reset, OUT
  fp4bit fp4bit_8 (.SAVE(demultiplexer_1_out7), .INPUT(in_1));  // open: reset, OUT
endmodule
