// Logisim project SD.circ as structural Verilog: 2 circuits, main circuit Mux2
module Mux2 (
  input  A,
  input  B,
  input  Sel,
  output out_4
);

  wire and_1_out, and_2_out;

  and and_1 (and_1_out, A, ~Sel);  // AND_Gate
  and and_2 (and_2_out, B, Sel);
  or or_1 (out_4, and_1_out, and_2_out);
endmodule

module Mux4 (
  input  A,
  input  B,
  input  C,
  input  D,
  input  SEL_0,
  input  SEL_1,
  output out_7
);

  wire mux2_1_out_4, mux2_2_out_4;

  Mux2 mux2_1 (.A(C), .B(D), .Sel(SEL_1), .out_4(mux2_1_out_4));
  Mux2 mux2_2 (.A(A), .B(B), .Sel(SEL_1), .out_4(mux2_2_out_4));
  Mux2 mux2_3 (.A(mux2_2_out_4), .B(mux2_1_out_4), .Sel(SEL_0), .out_4(out_7));
endmodule
