// Logisim project tentativa.circ as structural Verilog
module mux2 (
  input  A,
  input  B,
  input  Sel,
  output S
);

  wire and_1_out, and_2_out;

  and and_1 (and_1_out, A, ~Sel);  // AND_Gate
  and and_2 (and_2_out, B, Sel);
  or or_1 (S, and_1_out, and_2_out);
endmodule

module mux4 (
  input  A,
  input  B,
  input  C,
  input  D,
  input  Sel1,
  input  Sel0,
  output out_7
);

  wire mux2_1_s, mux2_2_s;

  mux2 mux2_1 (.A(A), .B(B), .Sel(Sel0), .S(mux2_1_s));
  mux2 mux2_2 (.A(C), .B(D), .Sel(Sel0), .S(mux2_2_s));
  mux2 mux2_3 (.A(mux2_1_s), .B(mux2_2_s), .Sel(Sel1), .S(out_7));
endmodule

module mux4b (
  input  in_1,
  input  in_2,
  input  in_3,
  input  in_4,
  input  [1:0] in_5,
  output out_6
);

  wire and_1_out, and_2_out, and_3_out, and_4_out;

  and and_1 (and_1_out, in_1, ~in_5[1], ~in_5[0]);  // AND_Gate
  and and_2 (and_2_out, in_2, ~in_5[1], in_5[0]);  // AND_Gate
  and and_3 (and_3_out, in_3, in_5[1], ~in_5[0]);  // AND_Gate
  and and_4 (and_4_out, in_4, in_5[1], in_5[0]);
  or or_1 (out_6, and_1_out, and_2_out, and_3_out, and_4_out);
endmodule

module somador (
  input  Vem1,
  input  a,
  input  b,
  output soma,
  output vai1
);

  Adder #(.width(1)) adder_1 (.a(a), .b(b), .out(soma), .cin(Vem1), .cout(vai1));
endmodule

module ULACell (
  input  b,
  input  a,
  input  Vem1,
  input  [2:0] OpCode,
  output saida,
  output Vai1
);

  wire and_1_out, or_1_out, somador_1_soma, xor_1_out;

  and and_1 (and_1_out, a, b);
  or or_1 (or_1_out, a, b);
  somador somador_1 (.a(a), .b(b), .Vem1(Vem1), .vai1(Vai1), .soma(somador_1_soma));
  xor xor_1 (xor_1_out, a, b);
  Multiplexer #(.select(3), .enable("false")) multiplexer_1 (
    .in0(and_1_out), .in1(or_1_out), .in2(somador_1_soma), .in3(xor_1_out), .in4(b), .in5(b), .in6(b),
    .out(saida), .sel(OpCode));  // open: in7
endmodule

module ULA (
  input  [31:0] A,
  input  [31:0] B,
  input  in_3,
  input  in_4,
  input  [2:0] ULAOpCode,
  output [31:0] Result
);

  wire slldetect_1_sll, ulacell_1_vai1, ulacell_3_vai1, ulacell_4_vai1, ulacell_5_vai1, ulacell_6_vai1,
       ulacell_7_vai1, ulacell_8_vai1, ulacell_9_vai1, ulacell_10_vai1, ulacell_11_vai1, ulacell_12_vai1,
       ulacell_13_vai1, ulacell_14_vai1, ulacell_15_vai1, ulacell_16_vai1, ulacell_17_vai1, ulacell_18_vai1,
       ulacell_19_vai1, ulacell_20_vai1, ulacell_21_vai1, ulacell_22_vai1, ulacell_23_vai1, ulacell_24_vai1,
       ulacell_25_vai1, ulacell_26_vai1, ulacell_27_vai1, ulacell_28_vai1, ulacell_29_vai1, ulacell_30_vai1,
       ulacell_31_vai1, ulacell_32_vai1;
  wire [31:0] shiftleftlogical1bit_1_out, shiftrightlogical1bit_1_out;
  wire [31:19] shiftrightarith1bit_1_out;

  ShiftRightLogical1bit shiftrightlogical1bit_1 (
    .In(shiftleftlogical1bit_1_out), .Shift(in_3), .Out(shiftrightlogical1bit_1_out));
  ShiftLeftLogical1bit shiftleftlogical1bit_1 (.In(B), .Shift(slldetect_1_sll), .Out(shiftleftlogical1bit_1_out));
  SLLDetect slldetect_1 (.ALUOpCode(ULAOpCode), .sll(slldetect_1_sll));
  ShiftRightArith1bit shiftrightarith1bit_1 (
    .In(shiftrightlogical1bit_1_out), .Shift(in_4),
    .Out({shiftrightarith1bit_1_out[31:30], {4{shiftrightarith1bit_1_out[30]}}, shiftrightarith1bit_1_out[25:23], {3{shiftrightarith1bit_1_out[23]}}, shiftrightarith1bit_1_out[19], {19{shiftrightarith1bit_1_out[23]}}}));
  ULACell ulacell_1 (
    .Vai1(ulacell_1_vai1), .b(shiftrightarith1bit_1_out[30]), .a(A[31]), .OpCode(ULAOpCode),
    .saida(Result[30]), .Vem1(ulacell_3_vai1));
  ULACell ulacell_2 (
    .b(shiftrightarith1bit_1_out[31]), .a(A[31]), .OpCode(ULAOpCode), .saida(Result[31]),
    .Vem1(ulacell_1_vai1));  // open: Vai1
  ULACell ulacell_3 (
    .Vai1(ulacell_3_vai1), .b(shiftrightarith1bit_1_out[30]), .a(A[31]), .OpCode(ULAOpCode),
    .saida(Result[29]), .Vem1(ulacell_4_vai1));
  ULACell ulacell_4 (
    .Vai1(ulacell_4_vai1), .b(shiftrightarith1bit_1_out[30]), .a(A[31]), .OpCode(ULAOpCode),
    .saida(Result[28]), .Vem1(ulacell_5_vai1));
  ULACell ulacell_5 (
    .Vai1(ulacell_5_vai1), .b(shiftrightarith1bit_1_out[30]), .a(A[31]), .OpCode(ULAOpCode),
    .saida(Result[27]), .Vem1(ulacell_7_vai1));
  ULACell ulacell_6 (
    .Vai1(ulacell_6_vai1), .b(shiftrightarith1bit_1_out[25]), .a(A[31]), .OpCode(ULAOpCode),
    .saida(Result[25]), .Vem1(ulacell_8_vai1));
  ULACell ulacell_7 (
    .Vai1(ulacell_7_vai1), .b(shiftrightarith1bit_1_out[30]), .a(A[31]), .OpCode(ULAOpCode),
    .saida(Result[26]), .Vem1(ulacell_6_vai1));
  ULACell ulacell_8 (
    .Vai1(ulacell_8_vai1), .b(shiftrightarith1bit_1_out[24]), .a(A[31]), .OpCode(ULAOpCode),
    .saida(Result[24]), .Vem1(ulacell_10_vai1));
  ULACell ulacell_9 (
    .Vai1(ulacell_9_vai1), .b(shiftrightarith1bit_1_out[23]), .a(A[31]), .OpCode(ULAOpCode),
    .saida(Result[22]), .Vem1(ulacell_12_vai1));
  ULACell ulacell_10 (
    .Vai1(ulacell_10_vai1), .b(shiftrightarith1bit_1_out[23]), .a(A[31]), .OpCode(ULAOpCode),
    .saida(Result[23]), .Vem1(ulacell_9_vai1));
  ULACell ulacell_11 (
    .Vai1(ulacell_11_vai1), .b(shiftrightarith1bit_1_out[23]), .a(A[31]), .OpCode(ULAOpCode),
    .saida(Result[20]), .Vem1(ulacell_13_vai1));
  ULACell ulacell_12 (
    .Vai1(ulacell_12_vai1), .b(shiftrightarith1bit_1_out[23]), .a(A[31]), .OpCode(ULAOpCode),
    .saida(Result[21]), .Vem1(ulacell_11_vai1));
  ULACell ulacell_13 (
    .Vai1(ulacell_13_vai1), .b(shiftrightarith1bit_1_out[23]), .a(A[31]), .OpCode(ULAOpCode),
    .saida(Result[19]), .Vem1(ulacell_14_vai1));
  ULACell ulacell_14 (
    .Vai1(ulacell_14_vai1), .b(shiftrightarith1bit_1_out[23]), .a(A[31]), .OpCode(ULAOpCode),
    .saida(Result[18]), .Vem1(ulacell_15_vai1));
  ULACell ulacell_15 (
    .Vai1(ulacell_15_vai1), .b(shiftrightarith1bit_1_out[23]), .a(A[31]), .OpCode(ULAOpCode),
    .saida(Result[17]), .Vem1(ulacell_16_vai1));
  ULACell ulacell_16 (
    .Vai1(ulacell_16_vai1), .b(shiftrightarith1bit_1_out[23]), .a(A[31]), .OpCode(ULAOpCode),
    .saida(Result[16]), .Vem1(ulacell_17_vai1));
  ULACell ulacell_17 (
    .Vai1(ulacell_17_vai1), .b(shiftrightarith1bit_1_out[23]), .a(A[31]), .OpCode(ULAOpCode),
    .saida(Result[15]), .Vem1(ulacell_18_vai1));
  ULACell ulacell_18 (
    .Vai1(ulacell_18_vai1), .b(shiftrightarith1bit_1_out[23]), .a(A[31]), .OpCode(ULAOpCode),
    .saida(Result[14]), .Vem1(ulacell_20_vai1));
  ULACell ulacell_19 (
    .Vai1(ulacell_19_vai1), .b(shiftrightarith1bit_1_out[23]), .a(A[10]), .OpCode(ULAOpCode),
    .saida(Result[12]), .Vem1(ulacell_21_vai1));
  ULACell ulacell_20 (
    .Vai1(ulacell_20_vai1), .b(shiftrightarith1bit_1_out[23]), .a(A[10]), .OpCode(ULAOpCode),
    .saida(Result[13]), .Vem1(ulacell_19_vai1));
  ULACell ulacell_21 (
    .Vai1(ulacell_21_vai1), .b(shiftrightarith1bit_1_out[23]), .a(A[10]), .OpCode(ULAOpCode),
    .saida(Result[11]), .Vem1(ulacell_22_vai1));
  ULACell ulacell_22 (
    .Vai1(ulacell_22_vai1), .b(shiftrightarith1bit_1_out[23]), .a(A[10]), .OpCode(ULAOpCode),
    .saida(Result[10]), .Vem1(ulacell_23_vai1));
  ULACell ulacell_23 (
    .Vai1(ulacell_23_vai1), .b(shiftrightarith1bit_1_out[23]), .a(A[10]), .OpCode(ULAOpCode),
    .saida(Result[9]), .Vem1(ulacell_24_vai1));
  ULACell ulacell_24 (
    .Vai1(ulacell_24_vai1), .b(shiftrightarith1bit_1_out[23]), .a(A[10]), .OpCode(ULAOpCode),
    .saida(Result[8]), .Vem1(ulacell_25_vai1));
  ULACell ulacell_25 (
    .Vai1(ulacell_25_vai1), .b(shiftrightarith1bit_1_out[23]), .a(A[10]), .OpCode(ULAOpCode),
    .saida(Result[7]), .Vem1(ulacell_26_vai1));
  ULACell ulacell_26 (
    .Vai1(ulacell_26_vai1), .b(shiftrightarith1bit_1_out[23]), .a(A[10]), .OpCode(ULAOpCode),
    .saida(Result[6]), .Vem1(ulacell_28_vai1));
  ULACell ulacell_27 (
    .Vai1(ulacell_27_vai1), .b(shiftrightarith1bit_1_out[23]), .a(A[10]), .OpCode(ULAOpCode),
    .saida(Result[4]), .Vem1(ulacell_29_vai1));
  ULACell ulacell_28 (
    .Vai1(ulacell_28_vai1), .b(shiftrightarith1bit_1_out[23]), .a(A[10]), .OpCode(ULAOpCode),
    .saida(Result[5]), .Vem1(ulacell_27_vai1));
  ULACell ulacell_29 (
    .Vai1(ulacell_29_vai1), .b(shiftrightarith1bit_1_out[23]), .a(A[10]), .OpCode(ULAOpCode),
    .saida(Result[3]), .Vem1(ulacell_30_vai1));
  ULACell ulacell_30 (
    .Vai1(ulacell_30_vai1), .b(shiftrightarith1bit_1_out[23]), .a(A[10]), .OpCode(ULAOpCode),
    .saida(Result[2]), .Vem1(ulacell_31_vai1));
  ULACell ulacell_31 (
    .Vai1(ulacell_31_vai1), .b(shiftrightarith1bit_1_out[23]), .a(A[1]), .OpCode(ULAOpCode),
    .saida(Result[1]), .Vem1(ulacell_32_vai1));
  ULACell ulacell_32 (
    .Vai1(ulacell_32_vai1), .b(shiftrightarith1bit_1_out[23]), .a(A[0]), .OpCode(ULAOpCode),
    .saida(Result[0]), .Vem1(1'b0));

  assign {A[30:11], A[9:2]} = {{20{A[31]}}, {8{A[10]}}};

  // Notes on the sheet:
  //   000 = and
  //   001 = or
  //   010 = soma
  //   011 = xor
  //   100 = sll
endmodule

module ShiftLeftLogical1bit (
  input  [31:0] In,
  input  Shift,
  output [31:0] Out
);

  Multiplexer #(.width(32), .enable("false")) multiplexer_1 (.in0(In), .in1({In[30:0], 1'b0}), .out(Out), .sel(Shift));
endmodule

module ShiftRightLogical1bit (
  input  [31:0] In,
  input  Shift,
  output [31:0] Out
);

  Multiplexer #(.width(32), .enable("false")) multiplexer_1 (.in0(In), .in1({1'b0, In[31:1]}), .out(Out), .sel(Shift));
endmodule

module ShiftRightArith1bit (
  input  [31:0] In,
  input  Shift,
  output [31:0] Out
);

  Multiplexer #(.width(32), .enable("false")) multiplexer_1 (
    .in0(In), .in1({{2{In[31]}}, In[30:1]}), .out(Out), .sel(Shift));
endmodule

module SLLDetect (
  input  [2:0] ALUOpCode,
  output sll
);

  and and_1 (sll, ~ALUOpCode[0], ~ALUOpCode[1], ALUOpCode[2]);  // AND_Gate
endmodule
